// Digital circuit IMMSRC.dig as structural Verilog
module IMMSRC (
  input  [2:0] ImmSrc,
  input  [24:0] Imm,
  output [23:0] ImmR
);

  wire [23:0] bitextender_1_out, bitextender_2_out, bitextender_3_out, bitextender_4_out;

  BitExtender #(.inputBits(12), .outputBits(24)) bitextender_1 (.in(Imm[24:13]), .out(bitextender_1_out));
  BitExtender #(.inputBits(13), .outputBits(24)) bitextender_2 (
    .in({Imm[24], Imm[0], Imm[23:18], Imm[4:1], 1'b0}), .out(bitextender_2_out));
  BitExtender #(.inputBits(12), .outputBits(24)) bitextender_3 (.in({Imm[24:18], Imm[4:0]}), .out(bitextender_3_out));
  BitExtender #(.inputBits(20), .outputBits(24)) bitextender_4 (
    .in({Imm[12:5], Imm[13], Imm[23:14], 1'b0}), .out(bitextender_4_out));
  Multiplexer #(.Selector_Bits(3), .Bits(24)) multiplexer_1 (
    .sel(ImmSrc), .in_0({24{1'b0}}), .in_1(bitextender_1_out), .in_2(bitextender_2_out),
    .in_3(bitextender_3_out), .in_4(bitextender_4_out), .in_5({24{1'b0}}), .in_6({24{1'b0}}),
    .in_7({24{1'b0}}), .out(ImmR));

  // Notes on the sheet:
  //   I
  //   B
  //   SW
  //   J
endmodule
