// Digital circuit pc+mi.dig as structural Verilog
module pc_mi (
  input  CLK
);

  wire memWrite, nand_1_out, PCSrc, RegWrite, uc_1_break, ula_1_gt, ula_1_lt, ula_1_zero, ULASrc;
  wire [1:0] resultSrc;
  wire [2:0] ImmSrc, ULAOp;
  wire [4:0] MI_d_2, MI_d_4, MI_d_5;
  wire [6:0] MI_d;
  wire [23:0] add_1_s, immsrc_1_immr, multiplexer_1_out, multiplexer_2_out, multiplexer_3_out, PC_plus_4_s,
       RA, ramdualport_1_d, registerfile_1_db, RS1, ula_1_ula_r;
  wire [24:5] MI_d_3;

  Multiplexer #(.Bits(24)) multiplexer_1 (.sel(PCSrc), .in_0(PC_plus_4_s), .in_1(add_1_s), .out(multiplexer_1_out));
  D_FF #(.Bits(24)) PC (.D(multiplexer_1_out), .C(CLK), .Q(RA));  // open: nQ
  IMMSRC immsrc_1 (.ImmSrc(ImmSrc), .Imm({MI_d_3[24:18], MI_d_5, MI_d_4, MI_d_3[7:5], MI_d_2}), .ImmR(immsrc_1_immr));
  Add #(.Bits(24)) PC_plus_4 (.a(RA), .b(24'h4), .c_i(1'b0), .s(PC_plus_4_s));  // open: c_o
  RegisterFile #(.AddrBits(5), .Bits(24)) registerfile_1 (
    .Din(multiplexer_3_out), .we(RegWrite), .Rw(MI_d_2), .C(CLK), .Ra(MI_d_4), .Rb(MI_d_5), .Da(RS1),
    .Db(registerfile_1_db));
  Multiplexer #(.Bits(24)) multiplexer_2 (
    .sel(ULASrc), .in_0(registerfile_1_db), .in_1(immsrc_1_immr), .out(multiplexer_2_out));
  ROM #(.AddrBits(24), .isProgramMemory("true"), .Bits(32)) MI (
    .A(RA), .sel(nand_1_out), .D({MI_d_3[24:18], MI_d_5, MI_d_4, MI_d_3[7:5], MI_d_2, MI_d}));
  ula ula_1 (
    .A1(RS1), .ULAOp(ULAOp), .A2(multiplexer_2_out), .LT(ula_1_lt), .ULA_R(ula_1_ula_r), .GT(ula_1_gt),
    .ZERO(ula_1_zero));
  Add #(.Bits(24)) add_1 (.a(multiplexer_3_out), .b(immsrc_1_immr), .c_i(1'b0), .s(add_1_s));  // open: c_o
  nand nand_1 (nand_1_out, 1'b1, uc_1_break);
  uc uc_1 (
    .instrucao({MI_d_3[24:18], MI_d_5, MI_d_4, MI_d_3[7:5], MI_d_2, MI_d}), .zero(ula_1_zero), .GT(ula_1_gt),
    .LT(ula_1_lt), .regWrite(RegWrite), .ImmSrc(ImmSrc), .memWrite(memWrite), .resultSrc(resultSrc),
    .ULASrc(ULASrc), .PCSrc(PCSrc), .ULAOp(ULAOp), .BREAK(uc_1_break));
  RAMDualPort #(.AddrBits(24), .Bits(24)) ramdualport_1 (
    .A(ula_1_ula_r), .Din(registerfile_1_db), .str(memWrite), .C(CLK), .ld(1'b1), .D(ramdualport_1_d));
  Multiplexer #(.Selector_Bits(2), .Bits(24)) multiplexer_3 (
    .sel(resultSrc), .in_0(ula_1_ula_r), .in_1(ramdualport_1_d), .in_2(RA), .in_3(RS1),
    .out(multiplexer_3_out));

  // Notes on the sheet:
  //   CLK: Hz: 5
  //   contents of MI (hex, n*v repeats v):
  //   1400493,0,0,0,513,0,0,0,48593,0,0,0,100613,0,0,0,100693,0,0,0
  //   ,8000ef,0,0,0,100073,0,0,0,c52023,0,0,0,d52223,0,0,0,200313,0,0,0
  //   ,2b35263,0,0,0,231393,0,0,0,a383b3,0,0,0,ffc3ae03,0,0,0,ff83ae83
  //   ,0,0,0,1de0f33,0,0,0,1e3a023,0,0,0,130313,0,0,0,fe1ff06f,0,0,0,4080e7
endmodule
