// Digital circuit qualehfuncao.dig as structural Verilog
module qualehfuncao (
  input  [6:0] OpCode,
  output R,
  output I,
  output B,
  output LW,
  output SW,
  output J,
  output JR,
  output E
);

  wire and_1_out, and_2_out, and_3_out, nor_1_out;

  and and_1 (and_1_out, OpCode[5], OpCode[6]);
  and and_2 (and_2_out, OpCode[2], ~OpCode[3], ~OpCode[4]);  // And
  and and_3 (and_3_out, OpCode[2], OpCode[3], ~OpCode[4]);  // And
  nor nor_1 (nor_1_out, OpCode[2], OpCode[4], OpCode[3]);
  and and_4 (E, OpCode[4], and_1_out);
  nor nor_2 (LW, OpCode[6], OpCode[5], OpCode[4]);
  and and_5 (SW, ~OpCode[6], OpCode[5], ~OpCode[4]);  // And
  and and_6 (R, ~OpCode[6], OpCode[5], OpCode[4]);  // And
  and and_7 (I, ~OpCode[6], ~OpCode[5], OpCode[4]);  // And
  and and_8 (JR, and_2_out, and_1_out);
  and and_9 (J, and_3_out, and_1_out);
  and and_10 (B, and_1_out, nor_1_out);
endmodule
