// Digital circuit registradores.dig as structural Verilog
module registradores (
  input  WE3,
  input  [4:0] A1,
  input  [4:0] A2,
  input  [4:0] A3,
  input  [23:0] WD3,
  input  clk,
  output [23:0] RD1,
  output [23:0] RD2
);

  wire C1, C2, C3, C4, C5, C6, C7, C8, C9, C10, C11, C12, C13, C14, C15, C16, C17, C18, C19, C20, C21, C22,
       C23, C24, C25, C26, C27, C28, C29, C30, C31, C32, w;
  wire [23:0] S1, S2, S3, S4, S5, S6, S7, S8, S9, S10, S11, S12, S13, S14, S15, S16, S17, S18, S19, S20, S21,
       S22, S23, S24, S25, S26, S27, S28, S29, S30, S31, S32;

  and and_1 (w, clk, WE3);
  Decoder #(.Selector_Bits(5)) decoder_1 (
    .sel(A3), .out_0(C1), .out_1(C2), .out_2(C3), .out_3(C4), .out_4(C5), .out_5(C6), .out_6(C7), .out_7(C8),
    .out_8(C9), .out_9(C10), .out_10(C11), .out_11(C12), .out_12(C13), .out_13(C14), .out_14(C15),
    .out_15(C16), .out_16(C17), .out_17(C18), .out_18(C19), .out_19(C20), .out_20(C21), .out_21(C22),
    .out_22(C23), .out_23(C24), .out_24(C25), .out_25(C26), .out_26(C27), .out_27(C28), .out_28(C29),
    .out_29(C30), .out_30(C31), .out_31(C32));
  Register #(.Bits(24)) register_1 (.D(WD3), .C(C1), .en(w), .Q(S1));
  Register #(.Bits(24)) register_2 (.D(WD3), .C(C2), .en(w), .Q(S2));
  Register #(.Bits(24)) register_3 (.D(WD3), .C(C3), .en(w), .Q(S3));
  Register #(.Bits(24)) register_4 (.D(WD3), .C(C4), .en(w), .Q(S4));
  Register #(.Bits(24)) register_5 (.D(WD3), .C(C5), .en(w), .Q(S5));
  Register #(.Bits(24)) register_6 (.D(WD3), .C(C6), .en(w), .Q(S6));
  Register #(.Bits(24)) register_7 (.D(WD3), .C(C7), .en(w), .Q(S7));
  Register #(.Bits(24)) register_8 (.D(WD3), .C(C8), .en(w), .Q(S8));
  Register #(.Bits(24)) register_9 (.D(WD3), .C(C9), .en(w), .Q(S9));
  Register #(.Bits(24)) register_10 (.D(WD3), .C(C10), .en(w), .Q(S10));
  Register #(.Bits(24)) register_11 (.D(WD3), .C(C11), .en(w), .Q(S11));
  Register #(.Bits(24)) register_12 (.D(WD3), .C(C12), .en(w), .Q(S12));
  Register #(.Bits(24)) register_13 (.D(WD3), .C(C13), .en(w), .Q(S13));
  Register #(.Bits(24)) register_14 (.D(WD3), .C(C14), .en(w), .Q(S14));
  Register #(.Bits(24)) register_15 (.D(WD3), .C(C15), .en(w), .Q(S15));
  Register #(.Bits(24)) register_16 (.D(WD3), .C(C16), .en(w), .Q(S16));
  Register #(.Bits(24)) register_17 (.D(WD3), .C(C17), .en(w), .Q(S17));
  Register #(.Bits(24)) register_18 (.D(WD3), .C(C18), .en(w), .Q(S18));
  Register #(.Bits(24)) register_19 (.D(WD3), .C(C19), .en(w), .Q(S19));
  Register #(.Bits(24)) register_20 (.D(WD3), .C(C20), .en(w), .Q(S20));
  Register #(.Bits(24)) register_21 (.D(WD3), .C(C21), .en(w), .Q(S21));
  Register #(.Bits(24)) register_22 (.D(WD3), .C(C22), .en(w), .Q(S22));
  Register #(.Bits(24)) register_23 (.D(WD3), .C(C23), .en(w), .Q(S23));
  Register #(.Bits(24)) register_24 (.D(WD3), .C(C24), .en(w), .Q(S24));
  Register #(.Bits(24)) register_25 (.D(WD3), .C(C25), .en(w), .Q(S25));
  Register #(.Bits(24)) register_26 (.D(WD3), .C(C26), .en(w), .Q(S26));
  Register #(.Bits(24)) register_27 (.D(WD3), .C(C27), .en(w), .Q(S27));
  Register #(.Bits(24)) register_28 (.D(WD3), .C(C28), .en(w), .Q(S28));
  Register #(.Bits(24)) register_29 (.D(WD3), .C(C29), .en(w), .Q(S29));
  Register #(.Bits(24)) register_30 (.D(WD3), .C(C30), .en(w), .Q(S30));
  Register #(.Bits(24)) register_31 (.D(WD3), .C(C31), .en(w), .Q(S31));
  Register #(.Bits(24)) register_32 (.D(WD3), .C(C32), .en(w), .Q(S32));
  Multiplexer #(.Selector_Bits(5), .Bits(24)) multiplexer_1 (
    .sel(A1), .in_0(S1), .in_1(S2), .in_2(S3), .in_3(S4), .in_4(S5), .in_5(S6), .in_6(S7), .in_7(S8),
    .in_8(S9), .in_9(S10), .in_10(S11), .in_11(S12), .in_12(S13), .in_13(S14), .in_14(S15), .in_15(S16),
    .in_16(S17), .in_17(S18), .in_18(S19), .in_19(S20), .in_20(S21), .in_21(S22), .in_22(S23), .in_23(S24),
    .in_24(S25), .in_25(S26), .in_26(S27), .in_27(S28), .in_28(S29), .in_29(S30), .in_30(S31), .in_31(S32),
    .out(RD1));
  Multiplexer #(.Selector_Bits(5), .Bits(24)) multiplexer_2 (
    .sel(A2), .in_0(S1), .in_1(S2), .in_2(S3), .in_3(S4), .in_4(S5), .in_5(S6), .in_6(S7), .in_7(S8),
    .in_8(S9), .in_9(S10), .in_10(S11), .in_11(S12), .in_12(S13), .in_13(S14), .in_14(S15), .in_15(S16),
    .in_16(S17), .in_17(S18), .in_18(S19), .in_19(S20), .in_20(S21), .in_21(S22), .in_22(S23), .in_23(S24),
    .in_24(S25), .in_25(S26), .in_26(S27), .in_27(S28), .in_28(S29), .in_29(S30), .in_30(S31), .in_31(S32),
    .out(RD2));

  // Notes on the sheet:
  //   ENTRADAS
  //   LEITURA
endmodule
