// Digital circuit uc.dig as structural Verilog
module uc (
  input  [31:0] instrucao,
  input  zero,
  input  GT,
  input  LT,
  output regWrite,
  output [2:0] ImmSrc,
  output memWrite,
  output [1:0] resultSrc,
  output ULASrc,
  output PCSrc,
  output [2:0] ULAOp,
  output BREAK
);

  wire and_1_out, j, multiplexer_1_out, not_1_out, or_1_out, or_5_out, qualehfuncao_1_b, qualehfuncao_1_i,
       qualehfuncao_1_jr, qualehfuncao_1_lw, qualehfuncao_1_r, uc_ula_1_add, uc_ula_1_and, uc_ula_1_or,
       uc_ula_1_shift, uc_ula_1_sub, uc_ula_1_xor;
  wire [1:0] B_T;

  qualehfuncao qualehfuncao_1 (
    .OpCode(instrucao[6:0]), .R(qualehfuncao_1_r), .I(qualehfuncao_1_i), .B(qualehfuncao_1_b),
    .LW(qualehfuncao_1_lw), .SW(memWrite), .J(ImmSrc[2]), .JR(qualehfuncao_1_jr), .E(BREAK));
  not not_1 (not_1_out, zero);
  or or_1 (or_1_out, GT, zero);
  uc_ula uc_ula_1 (
    .instrucao(instrucao[31:7]), .R(qualehfuncao_1_r), .I(qualehfuncao_1_i), .B(qualehfuncao_1_b),
    .LW(qualehfuncao_1_lw), .SW(memWrite), .JAL(ImmSrc[2]), .JALR(qualehfuncao_1_jr), .ADD(uc_ula_1_add),
    .SUB(uc_ula_1_sub), .XOR(uc_ula_1_xor), .OR(uc_ula_1_or), .AND(uc_ula_1_and), .SHIFT(uc_ula_1_shift),
    .B_T(B_T));
  or or_2 (ImmSrc[1], memWrite, qualehfuncao_1_b);
  nor nor_1 (regWrite, qualehfuncao_1_b, memWrite);
  or or_3 (resultSrc[0], qualehfuncao_1_lw, qualehfuncao_1_jr, memWrite);
  or or_4 (j, ImmSrc[2], qualehfuncao_1_jr);
  Multiplexer #(.Selector_Bits(2)) multiplexer_1 (
    .sel(B_T), .in_0(not_1_out), .in_1(zero), .in_2(LT), .in_3(or_1_out), .out(multiplexer_1_out));
  or or_5 (or_5_out, qualehfuncao_1_i, qualehfuncao_1_jr);
  and and_1 (and_1_out, multiplexer_1_out, qualehfuncao_1_b);
  PriorityEncoder #(.Selector_Bits(3)) priorityencoder_1 (
    .in0(uc_ula_1_add), .in1(uc_ula_1_sub), .in2(uc_ula_1_xor), .in3(uc_ula_1_or), .in4(uc_ula_1_and),
    .in5(uc_ula_1_shift), .in6(1'b0), .in7(1'b0), .num(ULAOp));  // open: any
  or or_6 (ImmSrc[0], or_5_out, resultSrc[0]);
  or or_7 (ULASrc, resultSrc[0], qualehfuncao_1_i, j);
  or or_8 (resultSrc[1], j, qualehfuncao_1_b);
  or or_9 (PCSrc, j, and_1_out);
endmodule
