// Digital circuit uc_ula.dig as structural Verilog
module uc_ula (
  input  [24:0] instrucao,
  input  R,
  input  I,
  input  B,
  input  LW,
  input  SW,
  input  JAL,
  input  JALR,
  output ADD,
  output SUB,
  output XOR,
  output OR,
  output AND,
  output SHIFT,
  output [1:0] B_T
);

  wire _0, _1, _2, _4, _5, _6, _7, and_1_out, and_2_out, and_3_out, and_5_out, and_6_out, and_10_out,
       demultiplexer_1_out_0, demultiplexer_1_out_1, demultiplexer_1_out_4, demultiplexer_1_out_5, or_1_out,
       or_2_out, or_4_out;

  Decoder #(.Selector_Bits(3)) decoder_1 (
    .sel(instrucao[7:5]), .out_0(_0), .out_1(_1), .out_2(_2), .out_4(_4), .out_5(_5), .out_6(_6), .out_7(_7));  // open: out_3
  or or_1 (or_1_out, R, I);
  and and_1 (and_1_out, _0, R);
  and and_2 (and_2_out, _0, I);
  or or_2 (or_2_out, LW, SW, JAL, JALR);
  and and_3 (and_3_out, B, 1'b1);
  Demultiplexer #(.Selector_Bits(3)) demultiplexer_1 (
    .sel(instrucao[7:5]), .in(and_3_out), .out_0(demultiplexer_1_out_0), .out_1(demultiplexer_1_out_1),
    .out_4(demultiplexer_1_out_4), .out_5(demultiplexer_1_out_5));  // open: out_2, out_3, out_6, out_7
  and and_4 (AND, _7, or_1_out);
  and and_5 (and_5_out, or_1_out, _2);
  and and_6 (and_6_out, ~instrucao[20], and_1_out);  // And
  and and_7 (OR, _6, or_1_out);
  or or_3 (ADD, and_6_out, and_2_out, or_2_out);
  and and_8 (XOR, _4, or_1_out);
  and and_9 (SHIFT, _1, or_1_out);
  and and_10 (and_10_out, ~and_6_out, and_1_out);  // And
  PriorityEncoder #(.Selector_Bits(2)) priorityencoder_1 (
    .in0(demultiplexer_1_out_0), .in1(demultiplexer_1_out_1), .in2(demultiplexer_1_out_4),
    .in3(demultiplexer_1_out_5), .num(B_T));  // open: any
  or or_4 (or_4_out, and_10_out, B);
  or or_5 (SUB, and_5_out, or_4_out);

  // Other names for the same wires on the sheet: func3[2:0] = instrucao[7:5]

  // Notes on the sheet:
  //   Funct7
endmodule
