// Digital circuit ula.dig as structural Verilog
module ula (
  input  [23:0] A1,
  input  [2:0] ULAOp,
  input  [23:0] A2,
  output LT,
  output [23:0] ULA_R,
  output GT,
  output ZERO
);

  wire [23:0] add_1_s, and_1_out, barrelshifter_1_out, or_1_out, sub_1_s, xor_1_out;

  Add #(.Bits(24)) add_1 (.a(A1), .b(A2), .c_i(1'b0), .s(add_1_s));  // open: c_o
  Sub #(.Bits(24)) sub_1 (.a(A1), .b(A2), .c_i(1'b0), .s(sub_1_s));  // open: c_o
  assign xor_1_out = A1 ^ A2;  // XOr xor_1, 24 bits wide
  assign or_1_out = A1 | A2;  // Or or_1, 24 bits wide
  assign and_1_out = A1 & A2;  // And and_1, 24 bits wide
  BarrelShifter #(.Bits(24)) barrelshifter_1 (.in(A1), .shift(A2[4:0]), .out(barrelshifter_1_out));
  Multiplexer #(.Selector_Bits(3), .Bits(24)) multiplexer_1 (
    .sel(ULAOp), .in_0(add_1_s), .in_1(sub_1_s), .in_2(xor_1_out), .in_3(or_1_out), .in_4(and_1_out),
    .in_5(barrelshifter_1_out), .in_6({24{1'b0}}), .in_7({24{1'b0}}), .out(ULA_R));
  zero zero_1 (.ula_out(ULA_R), .zero(ZERO));
  and and_2 (LT, ULA_R[23], ~ZERO);  // And
  and and_3 (GT, ~ULA_R[23], ~ZERO);  // And
endmodule
