// Digital circuit zero.dig as structural Verilog
module zero (
  input  [23:0] ula_out,
  output zero
);

  wire or_1_out, or_2_out, or_3_out, or_4_out, or_5_out, or_6_out, or_7_out, or_8_out, or_9_out, or_10_out,
       or_11_out, or_12_out, or_13_out, or_14_out, or_15_out, or_16_out, or_17_out, or_18_out, or_19_out,
       or_20_out, or_21_out, or_22_out;

  or or_1 (or_1_out, ula_out[0], ula_out[1]);
  or or_2 (or_2_out, ula_out[2], ula_out[3]);
  or or_3 (or_3_out, ula_out[4], ula_out[5]);
  or or_4 (or_4_out, ula_out[6], ula_out[7]);
  or or_5 (or_5_out, ula_out[8], ula_out[9]);
  or or_6 (or_6_out, ula_out[10], ula_out[11]);
  or or_7 (or_7_out, ula_out[12], ula_out[13]);
  or or_8 (or_8_out, ula_out[14], ula_out[15]);
  or or_9 (or_9_out, ula_out[16], ula_out[17]);
  or or_10 (or_10_out, ula_out[18], ula_out[19]);
  or or_11 (or_11_out, ula_out[20], ula_out[21]);
  or or_12 (or_12_out, ula_out[22], ula_out[23]);
  or or_13 (or_13_out, or_1_out, or_2_out);
  or or_14 (or_14_out, or_3_out, or_4_out);
  or or_15 (or_15_out, or_5_out, or_6_out);
  or or_16 (or_16_out, or_7_out, or_8_out);
  or or_17 (or_17_out, or_9_out, or_10_out);
  or or_18 (or_18_out, or_11_out, or_12_out);
  or or_19 (or_19_out, or_13_out, or_14_out);
  or or_20 (or_20_out, or_15_out, or_16_out);
  or or_21 (or_21_out, or_17_out, or_18_out);
  or or_22 (or_22_out, or_19_out, or_20_out);
  nor nor_1 (zero, or_22_out, or_21_out);
endmodule
